// Digital circuit 299_32bit.dig as structural Verilog
module _299_32bit (
  input  nMR,
  input  nOE2,
  input  nOE1,
  input  S_0,
  input  S_1,
  input  CP,
  input  DSR,
  input  DSL,
  output [31:0] I_O32,
  output Q31,
  output Q0
);

  wire _74299_1_q7, _74299_2_q0, _74299_2_q7, _74299_3_q0, _74299_3_q7, _74299_4_q0, bussplitter_1_d0,
       bussplitter_1_d1, bussplitter_1_d2, bussplitter_1_d3, bussplitter_1_d4, bussplitter_1_d5,
       bussplitter_1_d6, bussplitter_1_d7, bussplitter_1_d8, bussplitter_1_d9, bussplitter_1_d10,
       bussplitter_1_d11, bussplitter_1_d12, bussplitter_1_d13, bussplitter_1_d14, bussplitter_1_d15,
       bussplitter_1_d16, bussplitter_1_d17, bussplitter_1_d18, bussplitter_1_d19, bussplitter_1_d20,
       bussplitter_1_d21, bussplitter_1_d22, bussplitter_1_d23, bussplitter_1_d24, bussplitter_1_d25,
       bussplitter_1_d26, bussplitter_1_d27, bussplitter_1_d28, bussplitter_1_d29, bussplitter_1_d30,
       bussplitter_1_d31, or_1_out;

  BusSplitter #(.Bits(32)) bussplitter_1 (
    .D(I_O32), .OE(or_1_out), .D0(bussplitter_1_d0), .D1(bussplitter_1_d1), .D2(bussplitter_1_d2),
    .D3(bussplitter_1_d3), .D4(bussplitter_1_d4), .D5(bussplitter_1_d5), .D6(bussplitter_1_d6),
    .D7(bussplitter_1_d7), .D8(bussplitter_1_d8), .D9(bussplitter_1_d9), .D10(bussplitter_1_d10),
    .D11(bussplitter_1_d11), .D12(bussplitter_1_d12), .D13(bussplitter_1_d13), .D14(bussplitter_1_d14),
    .D15(bussplitter_1_d15), .D16(bussplitter_1_d16), .D17(bussplitter_1_d17), .D18(bussplitter_1_d18),
    .D19(bussplitter_1_d19), .D20(bussplitter_1_d20), .D21(bussplitter_1_d21), .D22(bussplitter_1_d22),
    .D23(bussplitter_1_d23), .D24(bussplitter_1_d24), .D25(bussplitter_1_d25), .D26(bussplitter_1_d26),
    .D27(bussplitter_1_d27), .D28(bussplitter_1_d28), .D29(bussplitter_1_d29), .D30(bussplitter_1_d30),
    .D31(bussplitter_1_d31));
  or or_1 (or_1_out, nOE1, nOE2);
  _74299 _74299_1 (
    .DSR(DSR), .S0(S_0), .S1(S_1), .CP(CP), .nOE1(nOE1), .nOE2(nOE2), .DSL(_74299_2_q0), .Q7(_74299_1_q7),
    .nMR(nMR), .I_O0(bussplitter_1_d0), .I_O1(bussplitter_1_d1), .I_O2(bussplitter_1_d2),
    .I_O3(bussplitter_1_d3), .I_O4(bussplitter_1_d4), .I_O5(bussplitter_1_d5), .I_O6(bussplitter_1_d6),
    .I_O7(bussplitter_1_d7), .Q0(Q0), .GND(1'b0), .VCC(1'b1));
  _74299 _74299_2 (
    .DSR(_74299_1_q7), .S0(S_0), .S1(S_1), .CP(CP), .nOE1(nOE1), .nOE2(nOE2), .DSL(_74299_3_q0),
    .Q7(_74299_2_q7), .nMR(nMR), .I_O0(bussplitter_1_d8), .I_O1(bussplitter_1_d9), .I_O2(bussplitter_1_d10),
    .I_O3(bussplitter_1_d11), .I_O4(bussplitter_1_d12), .I_O5(bussplitter_1_d13), .I_O6(bussplitter_1_d14),
    .I_O7(bussplitter_1_d15), .Q0(_74299_2_q0), .GND(1'b0), .VCC(1'b1));
  _74299 _74299_3 (
    .DSR(_74299_2_q7), .S0(S_0), .S1(S_1), .CP(CP), .nOE1(nOE1), .nOE2(nOE2), .DSL(_74299_4_q0),
    .Q7(_74299_3_q7), .nMR(nMR), .I_O0(bussplitter_1_d16), .I_O1(bussplitter_1_d17),
    .I_O2(bussplitter_1_d18), .I_O3(bussplitter_1_d19), .I_O4(bussplitter_1_d20), .I_O5(bussplitter_1_d21),
    .I_O6(bussplitter_1_d22), .I_O7(bussplitter_1_d23), .Q0(_74299_3_q0), .GND(1'b0), .VCC(1'b1));
  _74299 _74299_4 (
    .DSR(_74299_3_q7), .S0(S_0), .S1(S_1), .CP(CP), .nOE1(nOE1), .nOE2(nOE2), .DSL(DSL), .Q7(Q31), .nMR(nMR),
    .I_O0(bussplitter_1_d24), .I_O1(bussplitter_1_d25), .I_O2(bussplitter_1_d26), .I_O3(bussplitter_1_d27),
    .I_O4(bussplitter_1_d28), .I_O5(bussplitter_1_d29), .I_O6(bussplitter_1_d30), .I_O7(bussplitter_1_d31),
    .Q0(_74299_4_q0), .GND(1'b0), .VCC(1'b1));
endmodule
