// Digital circuit 382_32bit.dig as structural Verilog
module _382_32bit (
  input  S_0,
  input  S_1,
  input  S_2,
  input  [31:0] A,
  input  [31:0] B,
  input  C_in,
  output C_Out,
  output [31:0] F
);

  wire _74382_1_pin14, _74382_2_pin14, _74382_3_pin14, _74382_4_pin14, _74382_5_pin14, _74382_6_pin14,
       _74382_7_pin14;

  _74382 _74382_1 (
    .pin1(A[1]), .pin2(B[1]), .pin3(A[0]), .pin4(B[0]), .pin5(S_0), .pin6(S_1), .pin7(S_2), .pin8(F[0]),
    .pin9(F[1]), .pin10(1'b0), .pin11(F[2]), .pin12(F[3]), .pin14(_74382_1_pin14), .pin15(C_in),
    .pin16(B[3]), .pin17(A[3]), .pin18(B[2]), .pin19(A[2]), .pin20(1'b1));  // open: pin13
  _74382 _74382_2 (
    .pin1(A[5]), .pin2(B[5]), .pin3(A[4]), .pin4(B[4]), .pin5(S_0), .pin6(S_1), .pin7(S_2), .pin8(F[4]),
    .pin9(F[5]), .pin10(1'b0), .pin11(F[6]), .pin12(F[7]), .pin14(_74382_2_pin14), .pin15(_74382_1_pin14),
    .pin16(B[7]), .pin17(A[7]), .pin18(B[6]), .pin19(A[6]), .pin20(1'b1));  // open: pin13
  _74382 _74382_3 (
    .pin1(A[9]), .pin2(B[9]), .pin3(A[8]), .pin4(B[8]), .pin5(S_0), .pin6(S_1), .pin7(S_2), .pin8(F[8]),
    .pin9(F[9]), .pin10(1'b0), .pin11(F[10]), .pin12(F[11]), .pin14(_74382_3_pin14), .pin15(_74382_2_pin14),
    .pin16(B[11]), .pin17(A[11]), .pin18(B[10]), .pin19(A[10]), .pin20(1'b1));  // open: pin13
  _74382 _74382_4 (
    .pin1(A[13]), .pin2(B[13]), .pin3(A[12]), .pin4(B[12]), .pin5(S_0), .pin6(S_1), .pin7(S_2), .pin8(F[12]),
    .pin9(F[13]), .pin10(1'b0), .pin11(F[14]), .pin12(F[15]), .pin14(_74382_4_pin14), .pin15(_74382_3_pin14),
    .pin16(B[15]), .pin17(A[15]), .pin18(B[14]), .pin19(A[14]), .pin20(1'b1));  // open: pin13
  _74382 _74382_5 (
    .pin1(A[17]), .pin2(B[17]), .pin3(A[16]), .pin4(B[16]), .pin5(S_0), .pin6(S_1), .pin7(S_2), .pin8(F[16]),
    .pin9(F[17]), .pin10(1'b0), .pin11(F[18]), .pin12(F[19]), .pin14(_74382_5_pin14), .pin15(_74382_4_pin14),
    .pin16(B[19]), .pin17(A[19]), .pin18(B[18]), .pin19(A[18]), .pin20(1'b1));  // open: pin13
  _74382 _74382_6 (
    .pin1(A[21]), .pin2(B[21]), .pin3(A[20]), .pin4(B[20]), .pin5(S_0), .pin6(S_1), .pin7(S_2), .pin8(F[20]),
    .pin9(F[21]), .pin10(1'b0), .pin11(F[22]), .pin12(F[23]), .pin14(_74382_6_pin14), .pin15(_74382_5_pin14),
    .pin16(B[23]), .pin17(A[23]), .pin18(B[22]), .pin19(A[22]), .pin20(1'b1));  // open: pin13
  _74382 _74382_7 (
    .pin1(A[25]), .pin2(B[25]), .pin3(A[24]), .pin4(B[24]), .pin5(S_0), .pin6(S_1), .pin7(S_2), .pin8(F[24]),
    .pin9(F[25]), .pin10(1'b0), .pin11(F[26]), .pin12(F[27]), .pin14(_74382_7_pin14), .pin15(_74382_6_pin14),
    .pin16(B[27]), .pin17(A[27]), .pin18(B[26]), .pin19(A[26]), .pin20(1'b1));  // open: pin13
  _74382 _74382_8 (
    .pin1(A[29]), .pin2(B[29]), .pin3(A[28]), .pin4(B[28]), .pin5(S_0), .pin6(S_1), .pin7(S_2), .pin8(F[28]),
    .pin9(F[29]), .pin10(1'b0), .pin11(F[30]), .pin12(F[31]), .pin14(C_Out), .pin15(_74382_7_pin14),
    .pin16(B[31]), .pin17(A[31]), .pin18(B[30]), .pin19(A[30]), .pin20(1'b1));  // open: pin13

  // Notes on the sheet:
  //   S_0: pin 7
  //   S_1: pin 6
  //   S_2: pin 5
  //   C_Out: pin 4
  //   A: pin 1
  //   F: pin 8
  //   C_in: pin 2
endmodule
