// Digital circuit 8bit_193.dig as structural Verilog
module _8bit_193 (
  input  nCE,
  input  nU_D,
  input  nPL,
  input  CP,
  input  [7:0] D0_7,
  output nTCD,
  output nTCU,
  output [7:0] Q0_7
);

  wire _74191_1_pin13;

  _74191 _74191_1 (
    .pin1(D0_7[1]), .pin2(Q0_7[1]), .pin3(Q0_7[0]), .pin4(nCE), .pin5(nU_D), .pin6(Q0_7[2]), .pin7(Q0_7[3]),
    .pin8(1'b0), .pin9(D0_7[3]), .pin10(D0_7[2]), .pin11(nPL), .pin13(_74191_1_pin13), .pin14(CP),
    .pin15(D0_7[0]), .pin16(1'b1));  // open: pin12
  _74191 _74191_2 (
    .pin1(D0_7[5]), .pin2(Q0_7[5]), .pin3(Q0_7[4]), .pin4(nCE), .pin5(nU_D), .pin6(Q0_7[6]), .pin7(Q0_7[7]),
    .pin8(1'b0), .pin9(D0_7[7]), .pin10(D0_7[6]), .pin11(nPL), .pin12(nTCU), .pin13(nTCD),
    .pin14(_74191_1_pin13), .pin15(D0_7[4]), .pin16(1'b1));
endmodule
