// Digital circuit Sketch_v1.dig as structural Verilog
module Sketch_v1 (
);

  wire [7:0] SP_out;
  wire [11:0] pullup_1_out;
  wire [19:0] AP_q, driver_1_out, multiplexer_1_out, PC_out;
  wire [31:0] _382_s, A_q, B_q, barrelshifter_1_out, pulldown_1_out, register_1_q;

  // _74163 _74163_1: pin names not known
  CounterPreset #(.Bits(20)) PC (.in(driver_1_out), .out(PC_out));  // open: en, C, dir, ld, clr, ovf
  Register #(.Bits(20)) AP (.D(driver_1_out), .Q(AP_q));  // open: C, en
  CounterPreset #(.Bits(8)) SP (.in(driver_1_out[7:0]), .out(SP_out));  // open: en, C, dir, ld, clr, ovf
  // _74253 _74253_1: pin names not known
  PullUp #(.Bits(12)) pullup_1 (.out(pullup_1_out));
  Driver #(.Bits(20)) driver_1 (.in(PC_out), .out(driver_1_out));  // open: en
  Driver #(.Bits(20)) driver_2 (.in(AP_q), .out(driver_1_out));  // open: en
  Multiplexer #(.Selector_Bits(2), .Bits(20)) multiplexer_1 (
    .in_0(PC_out), .in_1(AP_q), .in_2({pullup_1_out, SP_out}), .in_3(B_q[19:0]), .out(multiplexer_1_out));  // open: sel
  PullDown #(.Bits(8)) pulldown_1 (.out(pulldown_1_out[7:0]));
  EEPROM #(.AddrBits(20), .Bits(32)) RAM (
    .A(multiplexer_1_out), .D({pulldown_1_out[11:0], driver_1_out}));  // open: CS, WE, OE
  Register #(.Bits(32)) IR (.D(pulldown_1_out));  // open: C, en, Q
  Register #(.Bits(32)) register_1 (.D({pulldown_1_out[11:0], driver_1_out}), .Q(register_1_q));  // open: C, en
  Register #(.Bits(32)) A (.D({pulldown_1_out[11:0], driver_1_out}), .Q(A_q));  // open: C, en
  BarrelShifter #(.Bits(32)) barrelshifter_1 (.in(register_1_q), .out(barrelshifter_1_out));  // open: shift
  Add #(.Bits(32)) _382 (.a(A_q), .b({pulldown_1_out[11:0], driver_1_out}), .s(_382_s));  // open: c_i, c_o
  Driver #(.Bits(32)) driver_3 (.in(barrelshifter_1_out), .out({pulldown_1_out[11:0], driver_1_out}));  // open: en
  Register #(.Bits(32)) B (.D(_382_s), .Q(B_q));  // open: C, en
  Driver #(.Bits(32)) driver_4 (.in(B_q), .out({pulldown_1_out[11:0], driver_1_out}));  // open: en
  // Pins of 20 and 32 bits meet at B_q
  // Pins of 12 and 32 bits meet at pulldown_1_out
  // Pins of 8 and 12 bits meet at pulldown_1_out[11:0]
endmodule
