// Digital circuit Sketch_v2.dig as structural Verilog
module Sketch_v2 (
  input  clk
);

  wire A_in, ALU_C, ALU_S0, ALU_S1, ALU_S2, ALUC, and_1_out, and_2_out, and_3_out, AP_in, AP_out, B_in,
       B_out, dipswitch_2_out, Flag_in, IN, IR_in, MCCR, MUX_0, MUX_1, not_1_out, not_2_out, not_3_out,
       not_4_out, OF, or_1_out, OUT, PC_en, PC_in, PC_out, pulldown_1_out, pullup_2_out, pullup_3_out, Q0,
       Q31, RAM_out, RAM_WE, reset, SF, Shift_L, Shift_out, Shift_R, Shift_reset, Shift_S1, Shift_S2, SP_EN,
       SP_in, SP_nrc, SP_tc, SP_UD, ZF;
  wire [3:0] MCC_out;
  wire [5:0] ALU_c_out;
  wire [7:0] IR_q, SP_q0_7;
  wire [11:0] pullup_1_out;
  wire [19:0] adrbus, AP_q, B_q, multiplexer_1_out, PC_out_2;
  wire [30:29] MC_d;
  wire [31:0] A_q, ALU_f, OUT_q;
  wire [31:20] B_q_2, Bus;

  _8bit_191 SP (
    .nCE(SP_EN), .nU_D(SP_UD), .nPL(SP_in), .CP(clk), .D0_7(adrbus[7:0]), .nRC(SP_nrc), .TC(SP_tc),
    .Q0_7(SP_q0_7));
  DipSwitch dipswitch_1 (.out(reset));
  PullDown pulldown_1 (.out(pulldown_1_out));
  CounterPreset #(.Bits(20)) PC (
    .en(PC_en), .C(clk), .dir(pulldown_1_out), .in(adrbus), .ld(~PC_in), .clr(~reset), .out(PC_out_2));  // open: ovf
  Register #(.Bits(20)) AP (.D(adrbus), .C(clk), .en(~AP_in), .Q(AP_q));
  PullUp #(.Bits(12)) pullup_1 (.out(pullup_1_out));
  not not_1 (not_1_out, PC_out);
  assign {Bus, adrbus} = not_1_out ? {{12{1'b0}}, PC_out_2} : 32'bz;  // Driver driver_1
  assign {Bus, adrbus} = not_3_out ? {{12{1'b0}}, AP_q} : 32'bz;  // Driver driver_2
  Multiplexer #(.Selector_Bits(2), .Bits(20)) multiplexer_1 (
    .sel({MUX_1, MUX_0}), .in_0(PC_out_2), .in_1(AP_q), .in_2({pullup_1_out, SP_q0_7}), .in_3(B_q),
    .out(multiplexer_1_out));
  not not_2 (not_2_out, IN);
  not not_3 (not_3_out, AP_out);
  DipSwitch dipswitch_2 (.out(dipswitch_2_out));
  or or_1 (or_1_out, RAM_WE, clk);
  assign {Bus, adrbus} = not_2_out ? 32'h64 : 32'bz;  // Driver driver_3
  EEPROM #(.AddrBits(20), .Bits(32)) RAM (
    .A(multiplexer_1_out), .CS(dipswitch_2_out), .WE(~or_1_out), .OE(~RAM_out), .D({Bus, adrbus}));
  Register #(.Bits(32)) u_OUT (.D({Bus, adrbus}), .C(clk), .en(~OUT), .Q(OUT_q));
  and and_1 (and_1_out, reset, MCCR);
  // Probe on OUT_q
  PullUp pullup_2 (.out(pullup_2_out));
  Counter #(.Bits(4)) MCC (.en(pullup_2_out), .C(clk), .clr(~and_1_out), .out(MCC_out));  // open: ovf
  Register #(.Bits(8)) IR (.D(Bus[31:24]), .C(clk), .en(~IR_in), .Q(IR_q));
  _299_32bit Shift (
    .nMR(Shift_reset), .nOE2(Shift_out), .nOE1(Shift_out), .S_0(Shift_S1), .S_1(Shift_S2), .CP(clk),
    .DSR(Shift_R), .DSL(Shift_L), .I_O32({Bus, adrbus}), .Q31(ALU_c_out[4]), .Q0(ALU_c_out[5]));
  EEPROM #(.AddrBits(16), .Bits(32)) MC (
    .A({4'b0000, IR_q, MCC_out}), .CS(pullup_3_out), .WE(1'b0), .OE(pullup_3_out),
    .D({MCCR, MC_d, IN, OUT, Shift_L, Shift_R, Shift_S2, Shift_S1, Shift_out, Shift_reset, Flag_in, RAM_WE, B_in, B_out, ALU_C, ALU_S2, ALU_S1, ALU_S0, A_in, SP_in, SP_UD, SP_EN, AP_in, AP_out, PC_out, PC_in, PC_en, MUX_1, MUX_0, IR_in, RAM_out}));
  PullUp pullup_3 (.out(pullup_3_out));
  // Probe on IR_q
  Register #(.Bits(32)) A (.D({Bus, adrbus}), .C(clk), .en(~A_in), .Q(A_q));
  _382_32bit ALU (
    .S_0(ALU_S0), .S_1(ALU_S1), .S_2(ALU_S2), .A(A_q), .B({Bus, adrbus}), .C_in(ALU_C), .C_Out(ALU_c_out[3]),
    .F(ALU_f));
  Comparator #(.Bits(32)) OR_2 (.a({32{1'b0}}), .b(ALU_f), .eq(ALU_c_out[0]));  // open: gt, lt
  Register #(.Bits(32)) B (.D(ALU_f), .C(clk), .en(~B_in), .Q({B_q_2, B_q}));
  not not_4 (not_4_out, B_out);
  assign {Bus, adrbus} = not_4_out ? {B_q_2, B_q} : 32'bz;  // Driver driver_4
  Register #(.Bits(6)) FLAG (
    .D({ALU_c_out[5:2], ALU_f[31], ALU_c_out[0]}), .C(clk), .en(~Flag_in), .Q({Q0, Q31, ALUC, OF, SF, ZF}));
  and and_2 (and_2_out, A_q[31], ~Bus[31], ~ALU_f[31]);  // And
  and and_3 (and_3_out, ~A_q[31], Bus[31], ALU_f[31]);  // And
  or or_3 (ALU_c_out[2], and_2_out, and_3_out);

  // Other names for the same wires on the sheet: Bus[19:0] = adrbus

  // Notes on the sheet:
  //   contents of RAM (hex, n*v repeats v):
  //   7f000005,2,6,3,f,8,9,0,0,0,55,0,aa,0,0,ff
  //   contents of MC (hex, n*v repeats v):
  //   987e1af0,187e1be3,987e1be3,987e1be3,987e1be3,987e1be3,987e1be3,987e1be3,987e1be3,
  //   987e1be3,987e1be3,987e1be3,987e1be3,987e1be3,987e1be3,987e1be3,987e1af0,987e1be3,
  //   987e1be3,987e1be3,987e1be3,987e1be3,987e1be3,987e1be3,987e1be3,987e1be3,987e1be3,
  //   987e1be3,987e1be3,987e1be3,987e1be3,987e1be3,987e1af0,987e1be3,987e1be3,987e1be3,
  //   987e1be3,987e1be3,987e1be3,987e1be3,987e1be3,987e1be3,987e1be3,987e1be3,987e1be3,
  //   987e1be3,987e1be3,987e1be3,987e1af0,987e1be3,987e1be3,987e1be3,987e1be3,987e1be3,
  //   987e1be3,987e1be3,987e1be3,987e1be3,987e1be3,987e1be3,987e1be3,987e1be3,987e1be3,
  //   987e1be3,987e1af0,987e1be3,987e1be3,987e1be3,987e1be3,987e1be3,987e1be3,987e1be3,
  //   987e1be3,987e1be3,987e1be3,987e1be3,987e1be3,987e1be3,987e1be3,987e1be3,987e1af0,
  //   987e1be3,987e1be3,987e1be3,987e1be3,987e1be3,987e1be3,987e1be3,987e1be3,987e1be3,
  //   987e1be3,987e1be3,987e1be3,987e1be3,987e1be3,987e1be3,987e1af0,987e1be3,987e1be3,
  //   987e1be3,987e1be3,987e1be3,987e1be3,987e1be3,987e1be3,987e1be3,987e1be3,987e1be3,
  //   987e1be3,987e1be3,987e1be3,987e1be3,987e1af0,987e1be3,987e1be3,987e1be3,987e1be3,
  //   987e1be3,987e1be3,987e1be3,987e1be3,987e1be3,987e1be3,987e1be3,987e1be3,987e1be3,
  //   987e1be3,987e1be3,987e1af0,987e1be3,987e1be3,987e1be3,987e1be3,987e1be3,987e1be3,
  //   987e1be3,987e1be3,987e1be3,987e1be3,987e1be3,987e1be3,987e1be3,987e1be3,987e1be3,
  //   987e1af0,987e1be3,987e1be3,987e1be3,987e1be3,987e1be3,987e1be3,987e1be3,987e1be3,
  //   987e1be3,987e1be3,987e1be3,987e1be3,987e1be3,987e1be3,987e1be3,987e1af0,987e1be3,
  //   987e1be3,987e1be3,987e1be3,987e1be3,987e1be3,987e1be3,987e1be3,987e1be3,987e1be3,
  //   987e1be3,987e1be3,987e1be3,987e1be3,987e1be3,987e1af0,987e1be3,987e1be3,987e1be3,
  //   987e1be3,987e1be3,987e1be3,987e1be3,987e1be3,987e1be3,987e1be3,987e1be3,987e1be3,
  //   987e1be3,987e1be3,987e1be3,987e1af0,987e1be3,987e1be3,987e1be3,987e1be3,987e1be3,
  //   987e1be3,987e1be3,987e1be3,987e1be3,987e1be3,987e1be3,987e1be3,987e1be3,987e1be3,
  //   987e1be3,987e1af0,987e1be3,987e1be3,987e1be3,987e1be3,987e1be3,987e1be3,987e1be3,
  //   987e1be3,987e1be3,987e1be3,987e1be3,987e1be3,987e1be3,987e1be3,987e1be3,987e1af0,
  //   987e1be3,987e1be3,987e1be3,987e1be3,987e1be3,987e1be3,987e1be3,987e1be3,987e1be3,
  //   987e1be3,987e1be3,987e1be3,987e1be3,987e1be3,987e1be3,987e1af0,987e1be3,987e1be3,
  //   987e1be3,987e1be3,987e1be3,987e1be3,987e1be3,987e1be3,987e1be3,987e1be3,987e1be3,
  //   987e1be3,987e1be3,987e1be3,987e1be3,987e1af0,987e1be3,987e1be3,987e1be3,987e1be3,
  //   987e1be3,987e1be3,987e1be3,987e1be3,987e1be3,987e1be3,987e1be3,987e1be3,987e1be3,
  //   987e1be3,987e1be3,987e1af0,987e1be3,987e1be3,987e1be3,987e1be3,987e1be3,987e1be3,
  //   987e1be3,987e1be3,987e1be3,987e1be3,987e1be3,987e1be3,987e1be3,987e1be3,987e1be3,
  //   987e1af0,987e1be3,987e1be3,987e1be3,987e1be3,987e1be3,987e1be3,987e1be3,987e1be3,
  //   987e1be3,987e1be3,987e1be3,987e1be3,987e1be3,987e1be3,987e1be3,987e1af0,987e1be3,
  //   987e1be3,987e1be3,987e1be3,987e1be3,987e1be3,987e1be3,987e1be3,987e1be3,987e1be3,
  //   987e1be3,987e1be3,987e1be3,987e1be3,987e1be3,987e1af0,987e1be3,987e1be3,987e1be3,
  //   987e1be3,987e1be3,987e1be3,987e1be3,987e1be3,987e1be3,987e1be3,987e1be3,987e1be3,
  //   987e1be3,987e1be3,987e1be3,987e1af0,987e1be3,987e1be3,987e1be3,987e1be3,987e1be3,
  //   987e1be3,987e1be3,987e1be3,987e1be3,987e1be3,987e1be3,987e1be3,987e1be3,987e1be3,
  //   987e1be3,987e1af0,987e1be3,987e1be3,987e1be3,987e1be3,987e1be3,987e1be3,987e1be3,
  //   987e1be3,987e1be3,987e1be3,987e1be3,987e1be3,987e1be3,987e1be3,987e1be3,987e1af0,
  //   987e1be3,987e1be3,987e1be3,987e1be3,987e1be3,987e1be3,987e1be3,987e1be3,987e1be3,
  //   987e1be3,987e1be3,987e1be3,987e1be3,987e1be3,987e1be3,987e1af0,987e1be3,987e1be3,
  //   987e1be3,987e1be3,987e1be3,987e1be3,987e1be3,987e1be3,987e1be3,987e1be3,987e1be3,
  //   987e1be3,987e1be3,987e1be3,987e1be3,987e1af0,987e1be3,987e1be3,987e1be3,987e1be3,
  //   987e1be3,987e1be3,987e1be3,987e1be3,987e1be3,987e1be3,987e1be3,987e1be3,987e1be3,
  //   987e1be3,987e1be3,987e1af0,987e1be3,987e1be3,987e1be3,987e1be3,987e1be3,987e1be3,
  //   987e1be3,987e1be3,987e1be3,987e1be3,987e1be3,987e1be3,987e1be3,987e1be3,987e1be3,
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  //   -ZF, SF, OF; CF(ALU), 2xCF(SHIFT)
endmodule
