// Digital circuit Sketch_v3.dig as structural Verilog
module Sketch_v3 (
  input  clk
);

  wire A_in, ALU_C, ALU_S0, ALU_S1, ALU_S2, and_1_out, and_2_out, and_3_out, AP_in, AP_out, B_in, B_out,
       CFLG, dipswitch_2_out, Flag_in, IN, IR_in, MCCR, MUX, not_1_out, not_2_out, not_3_out, not_4_out,
       or_1_out, OUT, PC_en, PC_in, PC_out, pulldown_1_out, pullup_1_out, pullup_2_out, RAM_out, RAM_WE,
       reset, Shift_L, Shift_out, Shift_R, Shift_reset, Shift_S1, Shift_S2;
  wire [3:0] MCC_out;
  wire [5:0] ALU_c_out, FLG;
  wire [7:0] IR_q;
  wire [19:0] adrbus, AP_q, multiplexer_1_out, PC_out_2;
  wire [30:25] MC_d;
  wire [31:0] A_q, ALU_f, B_q, OUT_q;
  wire [31:20] Bus;

  DipSwitch dipswitch_1 (.out(reset));
  PullDown pulldown_1 (.out(pulldown_1_out));
  CounterPreset #(.Bits(20)) PC (
    .en(PC_en), .C(clk), .dir(pulldown_1_out), .in(adrbus), .ld(~PC_in), .clr(~reset), .out(PC_out_2));  // open: ovf
  Register #(.Bits(20)) AP (.D(adrbus), .C(clk), .en(~AP_in), .Q(AP_q));
  not not_1 (not_1_out, PC_out);
  assign {Bus, adrbus} = not_1_out ? {{12{1'b0}}, PC_out_2} : 32'bz;  // Driver driver_1
  assign {Bus, adrbus} = not_3_out ? {{12{1'b0}}, AP_q} : 32'bz;  // Driver driver_2
  Multiplexer #(.Bits(20)) multiplexer_1 (.sel(MUX), .in_0(PC_out_2), .in_1(AP_q), .out(multiplexer_1_out));
  not not_2 (not_2_out, IN);
  not not_3 (not_3_out, AP_out);
  DipSwitch dipswitch_2 (.out(dipswitch_2_out));
  or or_1 (or_1_out, RAM_WE, clk);
  assign {Bus, adrbus} = not_2_out ? 32'h64 : 32'bz;  // Driver driver_3
  EEPROM #(.AddrBits(20), .Bits(32)) RAM (
    .A(multiplexer_1_out), .CS(dipswitch_2_out), .WE(~or_1_out), .OE(~RAM_out), .D({Bus, adrbus}));
  Register #(.Bits(32)) u_OUT (.D({Bus, adrbus}), .C(clk), .en(~OUT), .Q(OUT_q));
  and and_1 (and_1_out, reset, MCCR);
  // Probe on OUT_q
  PullUp pullup_1 (.out(pullup_1_out));
  Counter #(.Bits(4)) MCC (.en(pullup_1_out), .C(clk), .clr(~and_1_out), .out(MCC_out));  // open: ovf
  Register #(.Bits(8)) IR (.D(Bus[31:24]), .C(clk), .en(~IR_in), .Q(IR_q));
  _299_32bit Shift (
    .nMR(Shift_reset), .nOE2(Shift_out), .nOE1(Shift_out), .S_0(Shift_S1), .S_1(Shift_S2), .CP(clk),
    .DSR(Shift_R), .DSL(Shift_L), .I_O32({Bus, adrbus}), .Q31(ALU_c_out[4]), .Q0(ALU_c_out[5]));
  EEPROM #(.AddrBits(18), .Bits(32)) MC (
    .A({FLG[5:4], CFLG, FLG[2:0], IR_q, MCC_out}), .CS(pullup_2_out), .WE(1'b0), .OE(pullup_2_out),
    .D({MCCR, MC_d, IN, OUT, Shift_L, Shift_R, Shift_S2, Shift_S1, Shift_out, Shift_reset, Flag_in, RAM_WE, B_in, B_out, ALU_C, ALU_S2, ALU_S1, ALU_S0, A_in, AP_in, AP_out, PC_out, PC_in, PC_en, MUX, IR_in, RAM_out}));
  PullUp pullup_2 (.out(pullup_2_out));
  // Probe on IR_q
  Register #(.Bits(32)) A (.D({Bus, adrbus}), .C(clk), .en(~A_in), .Q(A_q));
  _382_32bit ALU (
    .S_0(ALU_S0), .S_1(ALU_S1), .S_2(ALU_S2), .A(A_q), .B({Bus, adrbus}), .C_in(ALU_C), .C_Out(ALU_c_out[3]),
    .F(ALU_f));
  Comparator #(.Bits(32)) OR_2 (.a({32{1'b0}}), .b(ALU_f), .eq(ALU_c_out[0]));  // open: gt, lt
  Register #(.Bits(32)) B (.D(ALU_f), .C(clk), .en(~B_in), .Q(B_q));
  not not_4 (not_4_out, B_out);
  assign {Bus, adrbus} = not_4_out ? B_q : 32'bz;  // Driver driver_4
  Register #(.Bits(6)) FLAG (
    .D({ALU_c_out[5:2], ALU_f[31], ALU_c_out[0]}), .C(clk), .en(~Flag_in), .Q({FLG[5:4], CFLG, FLG[2:0]}));
  and and_2 (and_2_out, A_q[31], ~Bus[31], ~ALU_f[31]);  // And
  and and_3 (and_3_out, ~A_q[31], Bus[31], ALU_f[31]);  // And
  or or_3 (ALU_c_out[2], and_2_out, and_3_out);

  // Other names for the same wires on the sheet: Bus[19:0] = adrbus; ZF = FLG[0]; SF = FLG[1]; OF = FLG[2];
  //   FLG[3] = CFLG; Q31 = FLG[4]; Q0 = FLG[5]

  // Notes on the sheet:
  //   contents of RAM (hex, n*v repeats v):
  //   1100000f,e,f,0,0,0,0,0,0,0,0,0,0,0,55,aa
  //   contents of MC (hex, n*v repeats v):
  //   8187e178,187e1f3,8187e1f3,8187e1f3,8187e1f3,8187e1f3,8187e1f3,8187e1f3,8187e1f3,8187e1f3,
  //   8187e1f3,8187e1f3,8187e1f3,8187e1f3,8187e1f3,8187e1f3,8187e178,187e1f3,8187e1f3,8187e1f3,
  //   8187e1f3,8187e1f3,8187e1f3,8187e1f3,8187e1f3,8187e1f3,8187e1f3,8187e1f3,8187e1f3,
  //   8187e1f3,8187e1f3,8187e1f3,8187e178,8187e1f3,8187e1f3,8187e1f3,8187e1f3,8187e1f3,
  //   8187e1f3,8187e1f3,8187e1f3,8187e1f3,8187e1f3,8187e1f3,8187e1f3,8187e1f3,8187e1f3,
  //   8187e1f3,8187e178,8187e1f3,8187e1f3,8187e1f3,8187e1f3,8187e1f3,8187e1f3,8187e1f3,
  //   8187e1f3,8187e1f3,8187e1f3,8187e1f3,8187e1f3,8187e1f3,8187e1f3,8187e1f3,8187e178,
  //   8187e1f3,8187e1f3,8187e1f3,8187e1f3,8187e1f3,8187e1f3,8187e1f3,8187e1f3,8187e1f3,
  //   8187e1f3,8187e1f3,8187e1f3,8187e1f3,8187e1f3,8187e1f3,8187e178,8187e1f3,8187e1f3,
  //   8187e1f3,8187e1f3,8187e1f3,8187e1f3,8187e1f3,8187e1f3,8187e1f3,8187e1f3,8187e1f3,
  //   8187e1f3,8187e1f3,8187e1f3,8187e1f3,8187e178,8187e1f3,8187e1f3,8187e1f3,8187e1f3,
  //   8187e1f3,8187e1f3,8187e1f3,8187e1f3,8187e1f3,8187e1f3,8187e1f3,8187e1f3,8187e1f3,
  //   8187e1f3,8187e1f3,8187e178,819fe0f6,8187a7fa,818741f7,183e1e3,8187e1f3,8187e1f3,8187e1f3,
  //   8187e1f3,8187e1f3,8187e1f3,8187e1f3,8187e1f3,8187e1f3,8187e1f3,8187e1f3,8187e178,
  //   187e1a3,8187e1f3,8187e1f3,8187e1f3,8187e1f3,8187e1f3,8187e1f3,8187e1f3,8187e1f3,8187e1f3,
  //   8187e1f3,8187e1f3,8187e1f3,8187e1f3,8187e1f3,8187e178,8187e1f3,8187e1f3,8187e1f3,
  //   8187e1f3,8187e1f3,8187e1f3,8187e1f3,8187e1f3,8187e1f3,8187e1f3,8187e1f3,8187e1f3,
  //   8187e1f3,8187e1f3,8187e1f3,8187e178,819fe1f6,8186e1f3,8187e1fb,187e1fb,8187e1f3,8187e1f3,
  //   8187e1f3,8187e1f3,8187e1f3,8187e1f3,8187e1f3,8187e1f3,8187e1f3,8187e1f3,8187e1f3,
  //   8187e178,8187e1f3,8187e1f3,8187e1f3,8187e1f3,8187e1f3,8187e1f3,8187e1f3,8187e1f3,
  //   8187e1f3,8187e1f3,8187e1f3,8187e1f3,8187e1f3,8187e1f3,8187e1f3,8187e178,8187e1f3,
  //   8187e1f3,8187e1f3,8187e1f3,8187e1f3,8187e1f3,8187e1f3,8187e1f3,8187e1f3,8187e1f3,
  //   8187e1f3,8187e1f3,8187e1f3,8187e1f3,8187e1f3,8187e178,8187e1f3,8187e1f3,8187e1f3,
  //   8187e1f3,8187e1f3,8187e1f3,8187e1f3,8187e1f3,8187e1f3,8187e1f3,8187e1f3,8187e1f3,
  //   8187e1f3,8187e1f3,8187e1f3,8187e178,8187e1f3,8187e1f3,8187e1f3,8187e1f3,8187e1f3,
  //   8187e1f3,8187e1f3,8187e1f3,8187e1f3,8187e1f3,8187e1f3,8187e1f3,8187e1f3,8187e1f3,
  //   8187e1f3,8187e178,8187e1f3,8187e1f3,8187e1f3,8187e1f3,8187e1f3,8187e1f3,8187e1f3,
  //   8187e1f3,8187e1f3,8187e1f3,8187e1f3,8187e1f3,8187e1f3,8187e1f3,8187e1f3,8187e178,
  //   8197e1f3,818361f7,8187e17a,819fe1f6,818fe1f3,18361f7,8187e1f3,8187e1f3,8187e1f3,8187e1f3,
  //   8187e1f3,8187e1f3,8187e1f3,8187e1f3,8187e1f3,8187e178,819fe1f6,8187e17a,8187e0f6,
  //   8187adf6,818361f7,8187e17a,18741f7,8187e1f3,8187e1f3,8187e1f3,8187e1f3,8187e1f3,8187e1f3,
  //   8187e1f3,8187e1f3,8187e178,8187e1f3,8187e1f3,8187e1f3,8187e1f3,8187e1f3,8187e1f3,
  //   8187e1f3,8187e1f3,8187e1f3,8187e1f3,8187e1f3,8187e1f3,8187e1f3,8187e1f3,8187e1f3,
  //   8187e178,8187e1f3,8187e1f3,8187e1f3,8187e1f3,8187e1f3,8187e1f3,8187e1f3,8187e1f3,
  //   8187e1f3,8187e1f3,8187e1f3,8187e1f3,8187e1f3,8187e1f3,8187e1f3,8187e178,8187e1f3,
  //   8187e1f3,8187e1f3,8187e1f3,8187e1f3,8187e1f3,8187e1f3,8187e1f3,8187e1f3,8187e1f3,
  //   8187e1f3,8187e1f3,8187e1f3,8187e1f3,8187e1f3,8187e178,8187e1f3,8187e1f3,8187e1f3,
  //   8187e1f3,8187e1f3,8187e1f3,8187e1f3,8187e1f3,8187e1f3,8187e1f3,8187e1f3,8187e1f3,
  //   8187e1f3,8187e1f3,8187e1f3,8187e178,8187e1f3,8187e1f3,8187e1f3,8187e1f3,8187e1f3,
  //   8187e1f3,8187e1f3,8187e1f3,8187e1f3,8187e1f3,8187e1f3,8187e1f3,8187e1f3,8187e1f3,
  //   8187e1f3,8187e178,8187e1f3,8187e1f3,8187e1f3,8187e1f3,8187e1f3,8187e1f3,8187e1f3,
  //   8187e1f3,8187e1f3,8187e1f3,8187e1f3,8187e1f3,8187e1f3,8187e1f3,8187e1f3,8187e178,
  //   8187e1f3,8187e1f3,8187e1f3,8187e1f3,8187e1f3,8187e1f3,8187e1f3,8187e1f3,8187e1f3,
  //   8187e1f3,8187e1f3,8187e1f3,8187e1f3,8187e1f3,8187e1f3,8187e178,8187e1f3,8187e1f3,
  //   8187e1f3,8187e1f3,8187e1f3,8187e1f3,8187e1f3,8187e1f3,8187e1f3,8187e1f3,8187e1f3,
  //   8187e1f3,8187e1f3,8187e1f3,8187e1f3,8187e178,8187e1f3,8187e1f3,8187e1f3,8187e1f3,
  //   8187e1f3,8187e1f3,8187e1f3,8187e1f3,8187e1f3,8187e1f3,8187e1f3,8187e1f3,8187e1f3,
  //   8187e1f3,8187e1f3,8187e178,8187e1f3,8187e1f3,8187e1f3,8187e1f3,8187e1f3,8187e1f3,
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  //   -ZF, SF, OF; CF(ALU), 2xCF(SHIFT)
endmodule
