// Digital circuit cpu_v1.dig as structural Verilog
module cpu_v1 (
  input  clk
);

  wire _74163_1_pin15, _74163_2_pin15, _74163_3_pin15, _74245_1_pin19, AP_pin2, AP_pin3, AP_pin4, AP_pin5,
       AP_pin6, AP_pin7, AP_pin8, AP_pin9, AP_pin12, AP_pin13, AP_pin14, AP_pin15, AP_pin16, AP_pin17,
       AP_pin18, dipswitch_1_out, dipswitch_2_out, LSB_pin9, LSB_pin15;
  wire [3:0] CNT16_19;
  wire [7:0] CNT0_7, CNT8_15;
  wire [11:0] eeprom_1_d;
  wire [19:0] BUS_ADR, eeprom_1_d_2;

  DipSwitch dipswitch_1 (.out(dipswitch_1_out));
  DipSwitch dipswitch_2 (.out(dipswitch_2_out));
  _74163 LSB (
    .pin1(dipswitch_1_out), .pin2(clk), .pin3(BUS_ADR[0]), .pin4(BUS_ADR[1]), .pin5(BUS_ADR[2]),
    .pin6(BUS_ADR[3]), .pin7(dipswitch_2_out), .pin8(1'b0), .pin9(LSB_pin9), .pin10(1'b1), .pin11(CNT0_7[3]),
    .pin12(CNT0_7[2]), .pin13(CNT0_7[1]), .pin14(CNT0_7[0]), .pin15(LSB_pin15), .pin16(1'b1));
  _74163 _74163_1 (
    .pin1(dipswitch_1_out), .pin2(clk), .pin3(BUS_ADR[4]), .pin4(BUS_ADR[5]), .pin5(BUS_ADR[6]),
    .pin6(BUS_ADR[7]), .pin7(dipswitch_2_out), .pin8(1'b0), .pin9(LSB_pin9), .pin10(LSB_pin15),
    .pin11(CNT0_7[7]), .pin12(CNT0_7[6]), .pin13(CNT0_7[5]), .pin14(CNT0_7[4]), .pin15(_74163_1_pin15),
    .pin16(1'b1));
  _74163 _74163_2 (
    .pin1(dipswitch_1_out), .pin2(clk), .pin3(BUS_ADR[8]), .pin4(BUS_ADR[9]), .pin5(BUS_ADR[10]),
    .pin6(BUS_ADR[11]), .pin7(dipswitch_2_out), .pin8(1'b0), .pin9(LSB_pin9), .pin10(_74163_1_pin15),
    .pin11(CNT8_15[3]), .pin12(CNT8_15[2]), .pin13(CNT8_15[1]), .pin14(CNT8_15[0]), .pin15(_74163_2_pin15),
    .pin16(1'b1));
  _74163 _74163_3 (
    .pin1(dipswitch_1_out), .pin2(clk), .pin3(BUS_ADR[12]), .pin4(BUS_ADR[13]), .pin5(BUS_ADR[14]),
    .pin6(BUS_ADR[15]), .pin7(dipswitch_2_out), .pin8(1'b0), .pin9(LSB_pin9), .pin10(_74163_2_pin15),
    .pin11(CNT8_15[7]), .pin12(CNT8_15[6]), .pin13(CNT8_15[5]), .pin14(CNT8_15[4]), .pin15(_74163_3_pin15),
    .pin16(1'b1));
  _74163 _74163_4 (
    .pin1(dipswitch_1_out), .pin2(clk), .pin3(BUS_ADR[16]), .pin4(BUS_ADR[17]), .pin5(BUS_ADR[18]),
    .pin6(BUS_ADR[19]), .pin7(dipswitch_2_out), .pin8(1'b0), .pin9(LSB_pin9), .pin10(_74163_3_pin15),
    .pin11(CNT16_19[3]), .pin12(CNT16_19[2]), .pin13(CNT16_19[1]), .pin14(CNT16_19[0]), .pin16(1'b1));  // open: pin15
  DipSwitch dipswitch_3 (.out(LSB_pin9));
  _74245 _74245_1 (
    .pin1(1'b1), .pin2(CNT0_7[0]), .pin3(CNT0_7[1]), .pin4(CNT0_7[2]), .pin5(CNT0_7[3]), .pin6(CNT0_7[4]),
    .pin7(CNT0_7[5]), .pin8(CNT0_7[6]), .pin9(CNT0_7[7]), .pin10(1'b0), .pin11(BUS_ADR[7]),
    .pin12(BUS_ADR[6]), .pin13(BUS_ADR[5]), .pin14(BUS_ADR[4]), .pin15(BUS_ADR[3]), .pin16(BUS_ADR[2]),
    .pin17(BUS_ADR[1]), .pin18(BUS_ADR[0]), .pin19(_74245_1_pin19), .pin20(1'b1));
  _74245 _74245_2 (
    .pin1(1'b1), .pin2(CNT8_15[0]), .pin3(CNT8_15[1]), .pin4(CNT8_15[2]), .pin5(CNT8_15[3]),
    .pin6(CNT8_15[4]), .pin7(CNT8_15[5]), .pin8(CNT8_15[6]), .pin9(CNT8_15[7]), .pin10(1'b0),
    .pin11(BUS_ADR[15]), .pin12(BUS_ADR[14]), .pin13(BUS_ADR[13]), .pin14(BUS_ADR[12]), .pin15(BUS_ADR[11]),
    .pin16(BUS_ADR[10]), .pin17(BUS_ADR[9]), .pin18(BUS_ADR[8]), .pin19(_74245_1_pin19), .pin20(1'b1));
  _74245 _74245_3 (
    .pin1(1'b1), .pin2(CNT16_19[0]), .pin3(CNT16_19[1]), .pin4(CNT16_19[2]), .pin5(CNT16_19[3]),
    .pin10(1'b0), .pin15(BUS_ADR[19]), .pin16(BUS_ADR[18]), .pin17(BUS_ADR[17]), .pin18(BUS_ADR[16]),
    .pin19(_74245_1_pin19), .pin20(1'b1));  // open: pin6, pin7, pin8, pin9, pin11, pin12, pin13, pin14
  DipSwitch dipswitch_4 (.out(_74245_1_pin19));
  // _74191 SP: pin names not known
  _74377 AP (
    .pin2(AP_pin2), .pin3(AP_pin3), .pin4(AP_pin4), .pin5(AP_pin5), .pin6(AP_pin6), .pin7(AP_pin7),
    .pin8(AP_pin8), .pin9(AP_pin9), .pin12(AP_pin12), .pin13(AP_pin13), .pin14(AP_pin14), .pin15(AP_pin15),
    .pin16(AP_pin16), .pin17(AP_pin17), .pin18(AP_pin18));  // open: pin1, pin10, pin11, pin19, pin20
  // _74377 _74377_1: pin names not known
  // _74377 _74377_2: pin names not known
  // _74191 _74191_1: pin names not known
  // _74245 _74245_4: pin names not known
  // _74245 _74245_5: pin names not known
  // _74245 _74245_6: pin names not known
  // _74253 MUX: pin names not known
  // _74253 _74253_1: pin names not known
  // _74253 _74253_2: pin names not known
  // _74253 _74253_3: pin names not known
  // _74253 _74253_4: pin names not known
  // _74253 _74253_5: pin names not known
  // _74253 _74253_6: pin names not known
  // _74253 _74253_7: pin names not known
  // _74253 _74253_8: pin names not known
  // _74253 _74253_9: pin names not known
  EEPROM #(.AddrBits(20), .Bits(32)) eeprom_1 (
    .A({20{1'b0}}), .CS(1'b0), .WE(1'b0), .OE(1'b0), .D({eeprom_1_d, eeprom_1_d_2}));
  // _74377 IR: pin names not known; wires that end beside it: {eeprom_1_d, eeprom_1_d_2}
  // _74377 _74377_3: pin names not known
  EEPROM MC ();  // open: A, CS, WE, OE, D
  // _74377 SHIFT: pin names not known
  // _74377 _74377_4: pin names not known
  // _74377 _74377_5: pin names not known
  // _74377 _74377_6: pin names not known
  // _74377 A: pin names not known
  // _74377 _74377_7: pin names not known
  // _74377 _74377_8: pin names not known
  // _74377 _74377_9: pin names not known
  // _74283 _74283_1: pin names not known
  // _74283 _74283_2: pin names not known
  // _74283 _74283_3: pin names not known
  // _74283 _74283_4: pin names not known
  // _74283 _74283_5: pin names not known
  // _74283 _74283_6: pin names not known
  // _74283 _74283_7: pin names not known
  // _74283 _74283_8: pin names not known
  // _74377 B: pin names not known
  // _74377 _74377_10: pin names not known
  // _74377 _74377_11: pin names not known
  // _74377 _74377_12: pin names not known
  // also tied to GND on the sheet: {eeprom_1_d[0], eeprom_1_d[1], eeprom_1_d[2], eeprom_1_d[3], eeprom_1_d[4], eeprom_1_d[5], eeprom_1_d[6], eeprom_1_d[7], eeprom_1_d[8], eeprom_1_d[9], eeprom_1_d[10], eeprom_1_d[11], eeprom_1_d_2[0], eeprom_1_d_2[1], eeprom_1_d_2[2], eeprom_1_d_2[3], eeprom_1_d_2[4], eeprom_1_d_2[5], eeprom_1_d_2[6], eeprom_1_d_2[7], eeprom_1_d_2[8], eeprom_1_d_2[9], eeprom_1_d_2[10], eeprom_1_d_2[11], eeprom_1_d_2[12], eeprom_1_d_2[13], eeprom_1_d_2[14], eeprom_1_d_2[15], eeprom_1_d_2[16], eeprom_1_d_2[17], eeprom_1_d_2[18], eeprom_1_d_2[19]}

  // Notes on the sheet:
  //   clk: Hz: 10000
endmodule
