// Digital circuit microcode.dig as structural Verilog
module microcode (
  input  clk
);

  wire pulldown_1_out, pullup_1_out;
  wire [3:0] counter_1_out;
  wire [7:0] eeprom_1_d;

  Seven_Seg_Hex seven_seg_hex_1 (.d(counter_1_out), .dp(pullup_1_out));
  Counter #(.Bits(4)) counter_1 (.en(pullup_1_out), .C(clk), .clr(eeprom_1_d[7]), .out(counter_1_out));  // open: ovf
  PullUp pullup_1 (.out(pullup_1_out));
  PullDown pulldown_1 (.out(pulldown_1_out));
  EEPROM #(.AddrBits(4), .Bits(8)) eeprom_1 (
    .A(counter_1_out), .CS(pullup_1_out), .WE(pulldown_1_out), .OE(pullup_1_out), .D(eeprom_1_d));

  // Notes on the sheet:
  //   contents of eeprom_1 (hex, n*v repeats v):
  //   0,0,0,0,0,ff
endmodule
