// Digital circuit test.dig as structural Verilog
module test (
);

  wire _382_32bit_1_c_out, A_out, and_1_out, and_2_out, and_3_out, and_4_out, and_7_out, and_8_out, B_out,
       dipswitch_65_out, dipswitch_66_out, dipswitch_67_out, dipswitch_68_out, dipswitch_69_out,
       dipswitch_70_out, dipswitch_71_out, dipswitch_72_out, dipswitch_73_out, dipswitch_74_out,
       dipswitch_75_out, dipswitch_76_out, dipswitch_77_out, dipswitch_110_out, dipswitch_111_out, F_out,
       or_1_out, Q0_out, Q7_out, S0_out, S1_out, undriven, xor_1_out;
  wire [1:0] and_5_out, register_1_q;
  wire [31:0] _299_32bit_1_i_o32, _382_32bit_1_f, dipswitch_1_out, dipswitch_33_out, dipswitch_78_out;

  DipSwitch dipswitch_1 (.out(dipswitch_1_out[0]));
  DipSwitch dipswitch_2 (.out(dipswitch_1_out[1]));
  DipSwitch dipswitch_3 (.out(dipswitch_1_out[2]));
  DipSwitch dipswitch_4 (.out(dipswitch_1_out[3]));
  DipSwitch dipswitch_5 (.out(dipswitch_1_out[4]));
  DipSwitch dipswitch_6 (.out(dipswitch_1_out[5]));
  DipSwitch dipswitch_7 (.out(dipswitch_1_out[6]));
  DipSwitch dipswitch_8 (.out(dipswitch_1_out[7]));
  DipSwitch dipswitch_9 (.out(dipswitch_1_out[8]));
  DipSwitch dipswitch_10 (.out(dipswitch_1_out[9]));
  DipSwitch dipswitch_11 (.out(dipswitch_1_out[10]));
  DipSwitch dipswitch_12 (.out(dipswitch_1_out[11]));
  DipSwitch dipswitch_13 (.out(dipswitch_1_out[12]));
  DipSwitch dipswitch_14 (.out(dipswitch_1_out[13]));
  DipSwitch dipswitch_15 (.out(dipswitch_1_out[14]));
  DipSwitch dipswitch_16 (.out(dipswitch_1_out[15]));
  DipSwitch dipswitch_17 (.out(dipswitch_1_out[16]));
  DipSwitch dipswitch_18 (.out(dipswitch_1_out[17]));
  DipSwitch dipswitch_19 (.out(dipswitch_1_out[18]));
  DipSwitch dipswitch_20 (.out(dipswitch_1_out[19]));
  DipSwitch dipswitch_21 (.out(dipswitch_1_out[20]));
  DipSwitch dipswitch_22 (.out(dipswitch_1_out[21]));
  DipSwitch dipswitch_23 (.out(dipswitch_1_out[22]));
  DipSwitch dipswitch_24 (.out(dipswitch_1_out[23]));
  DipSwitch dipswitch_25 (.out(dipswitch_1_out[24]));
  DipSwitch dipswitch_26 (.out(dipswitch_1_out[25]));
  DipSwitch dipswitch_27 (.out(dipswitch_1_out[26]));
  DipSwitch dipswitch_28 (.out(dipswitch_1_out[27]));
  DipSwitch dipswitch_29 (.out(dipswitch_1_out[28]));
  DipSwitch dipswitch_30 (.out(dipswitch_1_out[29]));
  DipSwitch dipswitch_31 (.out(dipswitch_1_out[30]));
  DipSwitch dipswitch_32 (.out(dipswitch_1_out[31]));
  DipSwitch dipswitch_33 (.out(dipswitch_33_out[0]));
  DipSwitch dipswitch_34 (.out(dipswitch_33_out[1]));
  DipSwitch dipswitch_35 (.out(dipswitch_33_out[2]));
  DipSwitch dipswitch_36 (.out(dipswitch_33_out[3]));
  DipSwitch dipswitch_37 (.out(dipswitch_33_out[4]));
  DipSwitch dipswitch_38 (.out(dipswitch_33_out[5]));
  DipSwitch dipswitch_39 (.out(dipswitch_33_out[6]));
  DipSwitch dipswitch_40 (.out(dipswitch_33_out[7]));
  DipSwitch dipswitch_41 (.out(dipswitch_33_out[8]));
  DipSwitch dipswitch_42 (.out(dipswitch_33_out[9]));
  DipSwitch dipswitch_43 (.out(dipswitch_33_out[10]));
  DipSwitch dipswitch_44 (.out(dipswitch_33_out[11]));
  DipSwitch dipswitch_45 (.out(dipswitch_33_out[12]));
  DipSwitch dipswitch_46 (.out(dipswitch_33_out[13]));
  DipSwitch dipswitch_47 (.out(dipswitch_33_out[14]));
  DipSwitch dipswitch_48 (.out(dipswitch_33_out[15]));
  DipSwitch dipswitch_49 (.out(dipswitch_33_out[16]));
  DipSwitch dipswitch_50 (.out(dipswitch_33_out[17]));
  DipSwitch dipswitch_51 (.out(dipswitch_33_out[18]));
  DipSwitch dipswitch_52 (.out(dipswitch_33_out[19]));
  DipSwitch dipswitch_53 (.out(dipswitch_33_out[20]));
  DipSwitch dipswitch_54 (.out(dipswitch_33_out[21]));
  DipSwitch dipswitch_55 (.out(dipswitch_33_out[22]));
  DipSwitch dipswitch_56 (.out(dipswitch_33_out[23]));
  DipSwitch dipswitch_57 (.out(dipswitch_33_out[24]));
  DipSwitch dipswitch_58 (.out(dipswitch_33_out[25]));
  DipSwitch dipswitch_59 (.out(dipswitch_33_out[26]));
  DipSwitch dipswitch_60 (.out(dipswitch_33_out[27]));
  DipSwitch dipswitch_61 (.out(dipswitch_33_out[28]));
  DipSwitch dipswitch_62 (.out(dipswitch_33_out[29]));
  DipSwitch dipswitch_63 (.out(dipswitch_33_out[30]));
  DipSwitch dipswitch_64 (.out(dipswitch_33_out[31]));
  _382_32bit _382_32bit_1 (
    .S_0(dipswitch_65_out), .S_1(dipswitch_66_out), .S_2(dipswitch_67_out), .A(dipswitch_1_out),
    .B(dipswitch_33_out), .C_in(dipswitch_68_out), .C_Out(_382_32bit_1_c_out), .F(_382_32bit_1_f));
  DipSwitch dipswitch_65 (.out(dipswitch_65_out));
  DipSwitch dipswitch_66 (.out(dipswitch_66_out));
  DipSwitch dipswitch_67 (.out(dipswitch_67_out));
  DipSwitch dipswitch_68 (.out(dipswitch_68_out));
  LED led_1 (.in(_382_32bit_1_f[0]));
  LED led_2 (.in(_382_32bit_1_f[1]));
  LED led_3 (.in(_382_32bit_1_f[2]));
  LED led_4 (.in(_382_32bit_1_f[3]));
  LED led_5 (.in(_382_32bit_1_f[4]));
  LED led_6 (.in(_382_32bit_1_f[5]));
  LED led_7 (.in(_382_32bit_1_f[6]));
  LED led_8 (.in(_382_32bit_1_f[7]));
  LED led_9 (.in(_382_32bit_1_f[8]));
  LED led_10 (.in(_382_32bit_1_f[9]));
  LED led_11 (.in(_382_32bit_1_f[10]));
  LED led_12 (.in(_382_32bit_1_f[11]));
  LED led_13 (.in(_382_32bit_1_f[12]));
  LED led_14 (.in(_382_32bit_1_f[13]));
  LED led_15 (.in(_382_32bit_1_f[14]));
  LED led_16 (.in(_382_32bit_1_f[15]));
  LED led_17 (.in(_382_32bit_1_f[16]));
  LED led_18 (.in(_382_32bit_1_f[17]));
  LED led_19 (.in(_382_32bit_1_f[18]));
  LED led_20 (.in(_382_32bit_1_f[19]));
  LED led_21 (.in(_382_32bit_1_f[20]));
  LED led_22 (.in(_382_32bit_1_f[21]));
  LED led_23 (.in(_382_32bit_1_f[22]));
  LED led_24 (.in(_382_32bit_1_f[23]));
  LED led_25 (.in(_382_32bit_1_f[24]));
  LED led_26 (.in(_382_32bit_1_f[25]));
  LED led_27 (.in(_382_32bit_1_f[26]));
  LED led_28 (.in(_382_32bit_1_f[27]));
  LED led_29 (.in(_382_32bit_1_f[28]));
  LED led_30 (.in(_382_32bit_1_f[29]));
  LED led_31 (.in(_382_32bit_1_f[30]));
  LED led_32 (.in(_382_32bit_1_f[31]));
  LED led_33 (.in(_382_32bit_1_c_out));
  _299_32bit _299_32bit_1 (
    .nMR(dipswitch_69_out), .nOE2(dipswitch_70_out), .nOE1(dipswitch_71_out), .S_0(dipswitch_72_out),
    .S_1(dipswitch_73_out), .CP(dipswitch_74_out), .DSR(dipswitch_75_out), .DSL(dipswitch_76_out),
    .I_O32(_299_32bit_1_i_o32));  // open: Q31, Q0
  DipSwitch dipswitch_69 (.out(dipswitch_69_out));
  DipSwitch dipswitch_70 (.out(dipswitch_70_out));
  DipSwitch dipswitch_71 (.out(dipswitch_71_out));
  DipSwitch dipswitch_72 (.out(dipswitch_72_out));
  DipSwitch dipswitch_73 (.out(dipswitch_73_out));
  DipSwitch dipswitch_74 (.out(dipswitch_74_out));
  DipSwitch dipswitch_75 (.out(dipswitch_75_out));
  DipSwitch dipswitch_76 (.out(dipswitch_76_out));
  DipSwitch dipswitch_77 (.out(dipswitch_77_out));
  DipSwitch dipswitch_78 (.out(dipswitch_78_out[0]));
  DipSwitch dipswitch_79 (.out(dipswitch_78_out[1]));
  DipSwitch dipswitch_80 (.out(dipswitch_78_out[2]));
  DipSwitch dipswitch_81 (.out(dipswitch_78_out[3]));
  DipSwitch dipswitch_82 (.out(dipswitch_78_out[4]));
  DipSwitch dipswitch_83 (.out(dipswitch_78_out[5]));
  DipSwitch dipswitch_84 (.out(dipswitch_78_out[6]));
  DipSwitch dipswitch_85 (.out(dipswitch_78_out[7]));
  DipSwitch dipswitch_86 (.out(dipswitch_78_out[8]));
  DipSwitch dipswitch_87 (.out(dipswitch_78_out[9]));
  DipSwitch dipswitch_88 (.out(dipswitch_78_out[10]));
  DipSwitch dipswitch_89 (.out(dipswitch_78_out[11]));
  DipSwitch dipswitch_90 (.out(dipswitch_78_out[12]));
  DipSwitch dipswitch_91 (.out(dipswitch_78_out[13]));
  DipSwitch dipswitch_92 (.out(dipswitch_78_out[14]));
  DipSwitch dipswitch_93 (.out(dipswitch_78_out[15]));
  DipSwitch dipswitch_94 (.out(dipswitch_78_out[16]));
  DipSwitch dipswitch_95 (.out(dipswitch_78_out[17]));
  DipSwitch dipswitch_96 (.out(dipswitch_78_out[18]));
  DipSwitch dipswitch_97 (.out(dipswitch_78_out[19]));
  DipSwitch dipswitch_98 (.out(dipswitch_78_out[20]));
  DipSwitch dipswitch_99 (.out(dipswitch_78_out[21]));
  DipSwitch dipswitch_100 (.out(dipswitch_78_out[22]));
  DipSwitch dipswitch_101 (.out(dipswitch_78_out[23]));
  DipSwitch dipswitch_102 (.out(dipswitch_78_out[24]));
  DipSwitch dipswitch_103 (.out(dipswitch_78_out[25]));
  DipSwitch dipswitch_104 (.out(dipswitch_78_out[26]));
  DipSwitch dipswitch_105 (.out(dipswitch_78_out[27]));
  DipSwitch dipswitch_106 (.out(dipswitch_78_out[28]));
  DipSwitch dipswitch_107 (.out(dipswitch_78_out[29]));
  DipSwitch dipswitch_108 (.out(dipswitch_78_out[30]));
  DipSwitch dipswitch_109 (.out(dipswitch_78_out[31]));
  assign _299_32bit_1_i_o32 = dipswitch_77_out ? dipswitch_78_out : 32'bz;  // Driver driver_1
  LED led_34 (.in(_299_32bit_1_i_o32[0]));
  LED led_35 (.in(_299_32bit_1_i_o32[1]));
  LED led_36 (.in(_299_32bit_1_i_o32[2]));
  LED led_37 (.in(_299_32bit_1_i_o32[3]));
  LED led_38 (.in(_299_32bit_1_i_o32[4]));
  LED led_39 (.in(_299_32bit_1_i_o32[5]));
  LED led_40 (.in(_299_32bit_1_i_o32[6]));
  LED led_41 (.in(_299_32bit_1_i_o32[7]));
  LED led_42 (.in(_299_32bit_1_i_o32[8]));
  LED led_43 (.in(_299_32bit_1_i_o32[9]));
  LED led_44 (.in(_299_32bit_1_i_o32[10]));
  LED led_45 (.in(_299_32bit_1_i_o32[11]));
  LED led_46 (.in(_299_32bit_1_i_o32[12]));
  LED led_47 (.in(_299_32bit_1_i_o32[13]));
  LED led_48 (.in(_299_32bit_1_i_o32[14]));
  LED led_49 (.in(_299_32bit_1_i_o32[15]));
  LED led_50 (.in(_299_32bit_1_i_o32[16]));
  LED led_51 (.in(_299_32bit_1_i_o32[17]));
  LED led_52 (.in(_299_32bit_1_i_o32[18]));
  LED led_53 (.in(_299_32bit_1_i_o32[19]));
  LED led_54 (.in(_299_32bit_1_i_o32[20]));
  LED led_55 (.in(_299_32bit_1_i_o32[21]));
  LED led_56 (.in(_299_32bit_1_i_o32[22]));
  LED led_57 (.in(_299_32bit_1_i_o32[23]));
  LED led_58 (.in(_299_32bit_1_i_o32[24]));
  LED led_59 (.in(_299_32bit_1_i_o32[25]));
  LED led_60 (.in(_299_32bit_1_i_o32[26]));
  LED led_61 (.in(_299_32bit_1_i_o32[27]));
  LED led_62 (.in(_299_32bit_1_i_o32[28]));
  LED led_63 (.in(_299_32bit_1_i_o32[29]));
  LED led_64 (.in(_299_32bit_1_i_o32[30]));
  LED led_65 (.in(_299_32bit_1_i_o32[31]));
  DipSwitch S0 (.out(S0_out));
  DipSwitch S1 (.out(S1_out));
  DipSwitch A (.out(A_out));
  DipSwitch B (.out(B_out));
  DipSwitch F (.out(F_out));
  and and_1 (and_1_out, A_out, ~B_out, ~F_out);  // And
  and and_2 (and_2_out, ~A_out, B_out, F_out);  // And
  xor xor_1 (xor_1_out, S0_out, S1_out);
  or or_1 (or_1_out, and_1_out, and_2_out);
  and and_3 (and_3_out, S0_out, xor_1_out);
  and and_4 (and_4_out, xor_1_out, S1_out);
  DipSwitch Q7 (.out(Q7_out));
  DipSwitch Q0 (.out(Q0_out));
  and and_5 (and_5_out[0], and_3_out, Q7_out);
  and and_6 (and_5_out[1], and_4_out, Q0_out);
  buf and_7 (and_7_out, ~undriven);  // And And open: In_2, In_3
  buf and_8 (and_8_out, undriven);  // And And open: In_2, In_3
  DipSwitch dipswitch_110 (.out(dipswitch_110_out));
  DipSwitch dipswitch_111 (.out(dipswitch_111_out));
  // Or or_2 has open pins: In_1=and_7_out, In_2=and_8_out, out=open
  Register #(.Bits(2)) register_1 (.D(and_5_out), .C(dipswitch_110_out), .en(dipswitch_111_out), .Q(register_1_q));
endmodule
